# Fritzing sketch LED cube (saved by Fritzing 0.9.2b)
circuit board: 13.1516cm x 7.97277cm
breadboards: 3

parts:
  atmega328P-PU = atmega328 [package=dip]
  R1 = Resistor [tolerance=±5% resistance=10k package=THT]
  XTAL1 = Crystal [frequency="16 Mhz" package=THT]
  R2 = Resistor [tolerance=±5% resistance=10k package=THT]
  C1 = Ceramic Capacitor [capacitance=22pF package="100 mil [THT, multilayer]"]
  C2 = Ceramic Capacitor [capacitance=22pF package="100 mil [THT, multilayer]"]
  74LS14P = SN74LS14N [package="DIP14 [THT]"]
  C3 = Electrolytic Capacitor [capacitance=10µF package="100 mil [THT, electrolytic]"]
  S1 = Pushbutton [package="[THT]"]
  S2 = Pushbutton [package="[THT]"]
  C4 = Electrolytic Capacitor [capacitance=10µF package="100 mil [THT, electrolytic]"]
  74HC595N = 74HC595 [package="DIP16 [THT]"]
  74HC595N_2 = 74HC595 [package="DIP16 [THT]"]
  U1 = Voltage Regulator - 5V [package="TO220 [THT]"]
  C5 = Electrolytic Capacitor [capacitance=10µF package="100 mil [THT, electrolytic]"]
  C6 = Electrolytic Capacitor [capacitance=10µF package="100 mil [THT, electrolytic]"]
  LED1 = LED - 5mm [color="Yellow (595nm)" package="5 mm [THT]"]
  LED2 = LED - 5mm [color="Yellow (595nm)" package="5 mm [THT]"]
  LED3 = LED - 5mm [color="Yellow (595nm)" package="5 mm [THT]"]
  LED4 = LED - 5mm [color="Yellow (595nm)" package="5 mm [THT]"]
  LED5 = LED - 5mm [color="Yellow (595nm)" package="5 mm [THT]"]
  LED6 = LED - 5mm [color="Yellow (595nm)" package="5 mm [THT]"]
  LED7 = LED - 5mm [color="Yellow (595nm)" package="5 mm [THT]"]
  LED8 = LED - 5mm [color="Yellow (595nm)" package="5 mm [THT]"]
  LED9 = LED - 5mm [color="Yellow (595nm)" package="5 mm [THT]"]
  LED10 = LED - 5mm [color="Yellow (595nm)" package="5 mm [THT]"]
  LED11 = LED - 5mm [color="Yellow (595nm)" package="5 mm [THT]"]
  LED12 = LED - 5mm [color="Yellow (595nm)" package="5 mm [THT]"]
  LED13 = LED - 5mm [color="Yellow (595nm)" package="5 mm [THT]"]
  LED14 = LED - 5mm [color="Yellow (595nm)" package="5 mm [THT]"]
  LED15 = LED - 5mm [color="Yellow (595nm)" package="5 mm [THT]"]
  LED16 = LED - 5mm [color="Yellow (595nm)" package="5 mm [THT]"]
  LED17 = LED - 5mm [color="Yellow (595nm)" package="5 mm [THT]"]
  LED18 = LED - 5mm [color="Yellow (595nm)" package="5 mm [THT]"]
  LED19 = LED - 5mm [color="Yellow (595nm)" package="5 mm [THT]"]
  LED20 = LED - 5mm [color="Yellow (595nm)" package="5 mm [THT]"]
  LED21 = LED - 5mm [color="Yellow (595nm)" package="5 mm [THT]"]
  LED22 = LED - 5mm [color="Yellow (595nm)" package="5 mm [THT]"]
  LED23 = LED - 5mm [color="Yellow (595nm)" package="5 mm [THT]"]
  LED24 = LED - 5mm [color="Yellow (595nm)" package="5 mm [THT]"]
  LED25 = LED - 5mm [color="Yellow (595nm)" package="5 mm [THT]"]
  LED26 = LED - 5mm [color="Yellow (595nm)" package="5 mm [THT]"]
  LED27 = LED - 5mm [color="Yellow (595nm)" package="5 mm [THT]"]
  Q1 = NPN-Transistor [package="TO92 [THT]"]
  Q2 = NPN-Transistor [package="TO92 [THT]"]
  Q3 = NPN-Transistor [package="TO92 [THT]"]
  Q4 = NPN-Transistor [package="TO92 [THT]"]
  Q5 = NPN-Transistor [package="TO92 [THT]"]
  Q6 = NPN-Transistor [package="TO92 [THT]"]
  Q7 = NPN-Transistor [package="TO92 [THT]"]
  Q8 = NPN-Transistor [package="TO92 [THT]"]
  Q9 = NPN-Transistor [package="TO92 [THT]"]
  Q10 = NPN-Transistor [package="TO92 [THT]"]
  Q11 = NPN-Transistor [package="TO92 [THT]"]
  Q12 = NPN-Transistor [package="TO92 [THT]"]
  R3 = Resistor [tolerance=±5% resistance=150 package=THT]
  R4 = Resistor [tolerance=±5% resistance=150 package=THT]
  R5 = Resistor [tolerance=±5% resistance=150 package=THT]
  R6 = Resistor [tolerance=±5% resistance=150 package=THT]
  R7 = Resistor [tolerance=±5% resistance=150 package=THT]
  R8 = Resistor [tolerance=±5% resistance=150 package=THT]
  R9 = Resistor [tolerance=±5% resistance=150 package=THT]
  R10 = Resistor [tolerance=±5% resistance=150 package=THT]
  R11 = Resistor [tolerance=±5% resistance=150 package=THT]
  R13 = Resistor [tolerance=±5% resistance=10k package=THT]
  R14 = Resistor [tolerance=±5% resistance=10k package=THT]
  R15 = Resistor [tolerance=±5% resistance=10k package=THT]
  R16 = Resistor [tolerance=±5% resistance=10k package=THT]
  R17 = Resistor [tolerance=±5% resistance=10k package=THT]
  R18 = Resistor [tolerance=±5% resistance=10k package=THT]
  R19 = Resistor [tolerance=±5% resistance=10k package=THT]
  R20 = Resistor [tolerance=±5% resistance=10k package=THT]
  R21 = Resistor [tolerance=±5% resistance=10k package=THT]
  R22 = Resistor [tolerance=±5% resistance=10k package=THT]
  R23 = Resistor [tolerance=±5% resistance=10k package=THT]
  R24 = Resistor [tolerance=±5% resistance=10k package=THT]
  R25 = Resistor [tolerance=±5% resistance=10k package=THT]
  R26 = Resistor [tolerance=±5% resistance=10k package=THT]
  VCC1 = Battery block 9V
  R27 = Rotary Potentiometer (Small) [maximum_resistance=100kΩ package=THT]

nets:
  N1: atmega328P-PU.RESET, R1.Pin_1
  N2: atmega328P-PU.D0_(RX), R2.Pin_0
  P2: atmega328P-PU.D2, 74LS14P.1Y
  P3: atmega328P-PU.D3_(PWM), 74LS14P.2Y
  N3: atmega328P-PU.GND#7, R2.Pin_1, C1.0, C2.0
  N4: atmega328P-PU.XLAT1, XTAL1.pin_0, C1.1
  N5: atmega328P-PU.XLAT2, XTAL1.pin_1, C2.1
  P8: atmega328P-PU.D8, 74HC595N.ST_CP, 74HC595N_2.ST_CP
  P11: atmega328P-PU.D11_(PWM), 74HC595N.DS
  P13: atmega328P-PU.D13, 74HC595N.SH_CP, 74HC595N_2.SH_CP
  5V: atmega328P-PU.AVCC, atmega328P-PU.AREF, R1.Pin_0, 74LS14P.VCC, 74HC595N.MR, 74HC595N.VCC, 74HC595N_2.MR, 74HC595N_2.VCC, U1.output_voltage, C6.+, R13.Pin_0, R14.Pin_0, R27.leg1
  GND: atmega328P-PU.GND#21, 74LS14P.GND, C3.-, S1.Pin_3, S1.Pin_4, S2.Pin_3, S2.Pin_4, C4.-, 74HC595N.GND, 74HC595N.OE, 74HC595N_2.GND, 74HC595N_2.OE, U1.GND, C5.-, C6.-, Q10.E, Q11.E, Q12.E, VCC1.-, R27.leg2
  N6: 74LS14P.1A, C3.+, S2.Pin_1, S2.Pin_2, R13.Pin_1
  N7: 74LS14P.2A, S1.Pin_1, S1.Pin_2, C4.+, R14.Pin_1
  T2: 74HC595N.Q1, R19.Pin_1
  T3: 74HC595N.Q2, R20.Pin_1
  T4: 74HC595N.Q3, R21.Pin_1
  T5: 74HC595N.Q4, R22.Pin_1
  T6: 74HC595N.Q5, R23.Pin_1
  T7: 74HC595N.Q6, R24.Pin_1
  T8: 74HC595N.Q7, R25.Pin_1
  N8: 74HC595N.Q7', 74HC595N_2.DS
  T1: 74HC595N.Q0, R18.Pin_1
  T10: 74HC595N_2.Q1, R17.Pin_1
  T11: 74HC595N_2.Q2, R16.Pin_1
  T12: 74HC595N_2.Q3, R15.Pin_1
  T9: 74HC595N_2.Q0, R26.Pin_1
  N9: U1.input_voltage, C5.+, VCC1.+
  N10: LED1.cathode, LED2.cathode, LED3.cathode, LED4.cathode, LED5.cathode, LED6.cathode, LED7.cathode, LED8.cathode, LED9.cathode, Q12.C
  N11: LED1.anode, LED10.anode, LED19.anode, Q2.E
  N12: LED2.anode, LED17.anode, LED26.anode, Q3.E
  N13: LED3.anode, LED18.anode, LED27.anode, Q4.E
  N14: LED4.anode, LED15.anode, LED24.anode, Q5.E
  N15: LED5.anode, LED13.anode, LED22.anode, Q8.E
  N16: LED6.anode, LED12.anode, LED21.anode, Q6.E
  N17: LED7.anode, LED16.anode, LED25.anode, Q7.E
  N18: LED8.anode, LED14.anode, LED23.anode, Q9.E
  N19: LED9.anode, LED11.anode, LED20.anode, Q1.E
  N20: LED10.cathode, LED11.cathode, LED12.cathode, LED13.cathode, LED14.cathode, LED15.cathode, LED16.cathode, LED17.cathode, LED18.cathode, Q11.C
  N21: LED19.cathode, LED20.cathode, LED21.cathode, LED22.cathode, LED23.cathode, LED24.cathode, LED25.cathode, LED26.cathode, LED27.cathode, Q10.C
  N22: Q1.B, R18.Pin_0
  N23: Q1.C, R3.Pin_0
  N24: Q2.B, R19.Pin_0
  N25: Q2.C, R4.Pin_0
  N26: Q3.B, R20.Pin_0
  N27: Q3.C, R5.Pin_0
  N28: Q4.B, R21.Pin_0
  N29: Q4.C, R6.Pin_0
  N30: Q5.B, R22.Pin_0
  N31: Q5.C, R7.Pin_0
  N32: Q6.B, R24.Pin_0
  N33: Q6.C, R10.Pin_0
  N34: Q7.B, R25.Pin_0
  N35: Q7.C, R8.Pin_0
  N36: Q8.B, R23.Pin_0
  N37: Q8.C, R9.Pin_0
  N38: Q9.B, R26.Pin_0
  N39: Q9.C, R11.Pin_0
  N40: Q10.B, R17.Pin_0
  N41: Q11.B, R16.Pin_0
  N42: Q12.B, R15.Pin_0
  N43: R3.Pin_1, R4.Pin_1, R5.Pin_1, R6.Pin_1, R7.Pin_1, R8.Pin_1, R9.Pin_1, R10.Pin_1, R11.Pin_1, R27.wiper
